# Fritzing sketch 回路 (saved by Fritzing 0.9.3b)
breadboards: 1

parts:
  パーツ1 = Arduino Nano (Rev3.0)
  NEOPIXEL1 = Neopixel Strip -- Black (30/m)
  U1 = TLP621 [package=THT]
  U2 = TLP621 [package=THT]
  U3 = TLP621 [package=THT]
  R1 = Resistor [tolerance=±5% resistance=220 package=THT]
  R2 = Resistor [tolerance=±5% resistance=220 package=THT]

nets:
  GND: パーツ1.GND, NEOPIXEL1.GND, U1.Pin_3, U2.Pin_1, U3.Pin_3
  N1: パーツ1.D2, NEOPIXEL1.DI
  N2: パーツ1.D5, U1.Pin_4
  N3: パーツ1.D6, U2.Pin_2
  N4: パーツ1.D7, U3.Pin_4
  N5: パーツ1.D8, R2.Pin_1
  N6: パーツ1.D9, R1.Pin_0
  5V: パーツ1.5V, NEOPIXEL1.+5V
  N7: R1.Pin_1, R2.Pin_0

custom parts:
  Neopixel Strip -- Black (30/m): Neopixel Strip, Black, 30 pixels per meter.
